# Fritzing sketch 3-12 (saved by Fritzing 0.5.2b)
breadboards: 1

parts:
  R1 = Resistor [resistance=220 package=THT]
  Q1 = NPN-Transistor [package="TO92 [THT]"]
  R2 = Resistor [resistance=220 package=THT]
  R3 = Resistor [resistance=220 package=THT]
  R4 = Resistor [resistance=220 package=THT]
  C1 = Ceramic Capacitor [capacitance=100nF rated_voltage=35V package="100 mil [THT, multilayer]"]
  C2 = Ceramic Capacitor [capacitance=100nF rated_voltage=35V package="100 mil [THT, multilayer]"]
  C3 = Ceramic Capacitor [capacitance=100nF rated_voltage=35V package="100 mil [THT, multilayer]"]
  C4 = Ceramic Capacitor [capacitance=100nF rated_voltage=35V package="100 mil [THT, multilayer]"]
  L1 = Inductor [package="400 mil [THT]"]
  C5 = Ceramic Capacitor [capacitance=100nF rated_voltage=35V package="100 mil [THT, multilayer]"]
  Q2 = NPN-Transistor [package="TO92 [THT]"]
  R5 = Resistor [resistance=220 package=THT]
  R6 = Resistor [resistance=220 package=THT]
  R7 = Resistor [resistance=220 package=THT]
  C6 = Ceramic Capacitor [capacitance=100nF rated_voltage=35V package="100 mil [THT, multilayer]"]
  R8 = Resistor [resistance=220 package=THT]
  C7 = Ceramic Capacitor [capacitance=100nF rated_voltage=35V package="100 mil [THT, multilayer]"]
  C8 = Tantalum Capacitor [capacitance=100nF rated_voltage=35V package="100 mil [THT, tantalum]"]
  VCC1 = obsolete Battery

nets:
  N1: R1.Pin_0, R4.Pin_0, Q2.C, R6.Pin_0, C7.1, C8.+, VCC1.+
  N2: R1.Pin_1, Q1.B, R2.Pin_0, C2.0, C4.0
  N3: Q1.E, R3.Pin_0, C1.1, C2.1, C3.0
  N4: Q1.C, R4.Pin_1, C3.1, L1.pin_0, C5.0
  GND: R2.Pin_1, R3.Pin_1, C1.0, R5.Pin_1, R7.Pin_1, R8.Pin_1, C7.0, C8.-, VCC1.-
  N5: C4.1, L1.pin_1
  N6: C5.1, Q2.B, R5.Pin_0, R6.Pin_1
  N7: Q2.E, R7.Pin_0, C6.0
  N8: C6.1, R8.Pin_0
