# Fritzing sketch p34测量放大器电路原理图面包版图 (saved by Fritzing 0.5.2b)
breadboards: 1

parts:
  U1 = LM 358 Dual Op-Amp [package="DIP8 [THT]"]
  VCC1 = obsolete Battery
  VCC2 = obsolete Battery
  R1 = Resistor [resistance=220 package=THT]
  R2 = Resistor [resistance=220 package=THT]
  R3 = Resistor [resistance=220 package=THT]
  U2 = LM 358 Dual Op-Amp [package="DIP8 [THT]"]
  R4 = Resistor [resistance=220 package=THT]
  R5 = Resistor [resistance=220 package=THT]
  R6 = Resistor [resistance=220 package=THT]
  R7 = Resistor [resistance=220 package=THT]
  R = Resistor [resistance=220 package=THT]
  R_2 = Resistor [resistance=220 package=THT]

nets:
  N1: U1.connector0, U1.connector1, U1.connector2, U1.connector3, VCC2.-, R1.Pin_0, R3.Pin_0, R3.Pin_1, U2.connector0, U2.connector1, U2.connector2, U2.connector3, R5.Pin_0, R_2.Pin_1
  N2: U1.connector4, U1.connector5, U1.connector6, U1.connector7, VCC1.+, R1.Pin_1, R2.Pin_0, R2.Pin_1, U2.connector4, U2.connector5, U2.connector6, U2.connector7, R4.Pin_0, R4.Pin_1, R5.Pin_1, R6.Pin_0, R6.Pin_1, R7.Pin_0, R.Pin_0
  N3: VCC1.-, VCC2.+, R7.Pin_1, R.Pin_1, R_2.Pin_0
