# Fritzing sketch 2-17 (saved by Fritzing 0.5.2b)
breadboards: 1

parts:
  D2 = Rectifier Diode [package="300 mil [THT]"]
  R1 = Resistor [resistance=1.5k package=THT]
  R2 = Resistor [resistance=47k package=THT]
  R3 = Resistor [resistance=47k package=THT]
  R4 = Resistor [resistance=47k package=THT]
  R4_2 = Resistor [resistance=47k package=THT]
  C1 = Ceramic Capacitor [capacitance=100nF rated_voltage=35V package="100 mil [THT, multilayer]"]
  C1_2 = Ceramic Capacitor [capacitance=100nF rated_voltage=35V package="100 mil [THT, multilayer]"]
  D1 = Rectifier Diode [package="300 mil [THT]"]

nets:
  N1: D2.cathode, R1.Pin_0, R2.Pin_1, D1.anode
  N2: D2.anode, R1.Pin_1, R4_2.Pin_1, D1.cathode
  N3: R2.Pin_0, R3.Pin_0
  N4: R3.Pin_1, C1_2.1
  GND: R4.Pin_0, R4_2.Pin_0, C1.0
  N5: R4.Pin_1, C1_2.0
