# Fritzing sketch P48二阶压控低通滤波器面包版图 (saved by Fritzing 0.5.2b)
breadboards: 1

parts:
  U1 = LM 358 Dual Op-Amp [package="DIP8 [THT]"]
  R3 = Resistor [resistance=220 package=THT]
  R4 = Resistor [resistance=220 package=THT]
  C = Ceramic Capacitor [capacitance=100nF rated_voltage=35V package="100 mil [THT, multilayer]"]
  R1 = Resistor [resistance=220 package=THT]
  R2 = Resistor [resistance=220 package=THT]
  C1 = Ceramic Capacitor [capacitance=100nF rated_voltage=35V package="100 mil [THT, multilayer]"]
  VCC1 = obsolete Battery
  VCC2 = obsolete Battery

nets:
  N1: U1.connector0, R4.Pin_0, C.1
  N2: U1.connector1, R3.Pin_1, R4.Pin_1
  N3: U1.connector2, R2.Pin_1, C1.0
  N4: U1.connector3, VCC2.-
  N5: U1.connector7, VCC1.+
  N6: R3.Pin_0, C1.1, VCC1.-, VCC2.+
  N7: C.0, R1.Pin_1, R2.Pin_0
